# Fritzing sketch shift_register_x2_led_x10_x4-1 (saved by Fritzing 0.9.3b)
breadboards: 4

parts:
  パーツ1 = Arduino Uno (Rev3)
  U1 = 74HC595 [package="DIP16 [THT]"]
  U2 = 74HC595 [package="DIP16 [THT]"]
  R1 = Resistor [tolerance=±5% resistance=150 package=THT]
  R2 = Resistor [tolerance=±5% resistance=150 package=THT]
  R3 = Resistor [tolerance=±5% resistance=150 package=THT]
  R4 = Resistor [tolerance=±5% resistance=150 package=THT]
  R5 = Resistor [tolerance=±5% resistance=150 package=THT]
  R6 = Resistor [tolerance=±5% resistance=150 package=THT]
  R7 = Resistor [tolerance=±5% resistance=150 package=THT]
  R8 = Resistor [tolerance=±5% resistance=150 package=THT]
  R9 = Resistor [tolerance=±5% resistance=150 package=THT]
  R10 = Resistor [tolerance=±5% resistance=150 package=THT]
  R11 = Resistor [tolerance=±5% resistance=150 package=THT]
  R12 = Resistor [tolerance=±5% resistance=150 package=THT]
  R13 = Resistor [tolerance=±5% resistance=150 package=THT]
  R14 = Resistor [tolerance=±5% resistance=150 package=THT]
  R15 = Resistor [tolerance=±5% resistance=150 package=THT]
  R16 = Resistor [tolerance=±5% resistance=150 package=THT]
  R17 = Resistor [tolerance=±5% resistance=150 package=THT]
  R18 = Resistor [tolerance=±5% resistance=150 package=THT]
  U3 = 74HC595 [package="DIP16 [THT]"]
  U4 = 74HC595 [package="DIP16 [THT]"]
  R19 = Resistor [tolerance=±5% resistance=150 package=THT]
  R20 = Resistor [tolerance=±5% resistance=150 package=THT]
  R21 = Resistor [tolerance=±5% resistance=150 package=THT]
  R22 = Resistor [tolerance=±5% resistance=150 package=THT]
  R23 = Resistor [tolerance=±5% resistance=150 package=THT]
  R24 = Resistor [tolerance=±5% resistance=150 package=THT]
  R25 = Resistor [tolerance=±5% resistance=150 package=THT]
  R26 = Resistor [tolerance=±5% resistance=150 package=THT]
  R27 = Resistor [tolerance=±5% resistance=150 package=THT]
  R28 = Resistor [tolerance=±5% resistance=150 package=THT]
  U5 = 74HC595 [package="DIP16 [THT]"]
  U6 = 74HC595 [package="DIP16 [THT]"]
  R29 = Resistor [tolerance=±5% resistance=150 package=THT]
  R30 = Resistor [tolerance=±5% resistance=150 package=THT]
  R31 = Resistor [tolerance=±5% resistance=150 package=THT]
  R32 = Resistor [tolerance=±5% resistance=150 package=THT]
  R33 = Resistor [tolerance=±5% resistance=150 package=THT]
  R34 = Resistor [tolerance=±5% resistance=150 package=THT]
  R35 = Resistor [tolerance=±5% resistance=150 package=THT]
  R36 = Resistor [tolerance=±5% resistance=150 package=THT]
  R37 = Resistor [tolerance=±5% resistance=150 package=THT]
  R38 = Resistor [tolerance=±5% resistance=150 package=THT]
  U7 = 74HC595 [package="DIP16 [THT]"]
  U8 = 74HC595 [package="DIP16 [THT]"]
  R39 = Resistor [tolerance=±5% resistance=150 package=THT]
  R40 = Resistor [tolerance=±5% resistance=150 package=THT]
  LED1 = LED - 3mm [color="Red (633nm)" package="3 mm [THT]"]
  LED2 = LED - 3mm [color="Red (633nm)" package="3 mm [THT]"]
  LED3 = LED - 3mm [color="Red (633nm)" package="3 mm [THT]"]
  LED4 = LED - 3mm [color="Red (633nm)" package="3 mm [THT]"]
  LED5 = LED - 3mm [color="Red (633nm)" package="3 mm [THT]"]
  LED6 = LED - 3mm [color="Red (633nm)" package="3 mm [THT]"]
  LED7 = LED - 3mm [color="Red (633nm)" package="3 mm [THT]"]
  LED8 = LED - 3mm [color="Red (633nm)" package="3 mm [THT]"]
  LED9 = LED - 3mm [color="Red (633nm)" package="3 mm [THT]"]
  LED10 = LED - 3mm [color="Red (633nm)" package="3 mm [THT]"]
  LED11 = LED - 3mm [color="Red (633nm)" package="3 mm [THT]"]
  LED12 = LED - 3mm [color="Red (633nm)" package="3 mm [THT]"]
  LED13 = LED - 3mm [color="Red (633nm)" package="3 mm [THT]"]
  LED14 = LED - 3mm [color="Red (633nm)" package="3 mm [THT]"]
  LED15 = LED - 3mm [color="Red (633nm)" package="3 mm [THT]"]
  LED16 = LED - 3mm [color="Red (633nm)" package="3 mm [THT]"]
  LED17 = LED - 3mm [color="Red (633nm)" package="3 mm [THT]"]
  LED18 = LED - 3mm [color="Red (633nm)" package="3 mm [THT]"]
  LED19 = LED - 3mm [color="Red (633nm)" package="3 mm [THT]"]
  LED20 = LED - 3mm [color="Red (633nm)" package="3 mm [THT]"]
  LED21 = LED - 3mm [color="Red (633nm)" package="3 mm [THT]"]
  LED22 = LED - 3mm [color="Red (633nm)" package="3 mm [THT]"]
  LED23 = LED - 3mm [color="Red (633nm)" package="3 mm [THT]"]
  LED24 = LED - 3mm [color="Red (633nm)" package="3 mm [THT]"]
  LED25 = LED - 3mm [color="Red (633nm)" package="3 mm [THT]"]
  LED26 = LED - 3mm [color="Red (633nm)" package="3 mm [THT]"]
  LED27 = LED - 3mm [color="Red (633nm)" package="3 mm [THT]"]
  LED28 = LED - 3mm [color="Red (633nm)" package="3 mm [THT]"]
  LED29 = LED - 3mm [color="Red (633nm)" package="3 mm [THT]"]
  LED30 = LED - 3mm [color="Red (633nm)" package="3 mm [THT]"]
  LED31 = LED - 3mm [color="Red (633nm)" package="3 mm [THT]"]
  LED32 = LED - 3mm [color="Red (633nm)" package="3 mm [THT]"]
  LED33 = LED - 3mm [color="Red (633nm)" package="3 mm [THT]"]
  LED34 = LED - 3mm [color="Red (633nm)" package="3 mm [THT]"]
  LED35 = LED - 3mm [color="Red (633nm)" package="3 mm [THT]"]
  LED36 = LED - 3mm [color="Red (633nm)" package="3 mm [THT]"]
  LED37 = LED - 3mm [color="Red (633nm)" package="3 mm [THT]"]
  LED38 = LED - 3mm [color="Red (633nm)" package="3 mm [THT]"]
  LED39 = LED - 3mm [color="Red (633nm)" package="3 mm [THT]"]
  LED40 = LED - 3mm [color="Red (633nm)" package="3 mm [THT]"]

nets:
  N1: パーツ1.D8, U3.DS
  N2: パーツ1.D9_PWM, U3.SH_CP, U4.SH_CP
  N3: パーツ1.D10_PWM/SS, U3.ST_CP, U4.ST_CP
  N4: パーツ1.D11_PWM/MOSI, U7.DS
  N5: パーツ1.D12/MISO, U7.SH_CP, U8.SH_CP
  N6: パーツ1.D13/SCK, U7.ST_CP, U8.ST_CP
  N7: パーツ1.D2, U1.DS
  N8: パーツ1.D3_PWM, U1.SH_CP, U2.SH_CP
  N9: パーツ1.D4, U1.ST_CP, U2.ST_CP
  N10: パーツ1.D5_PWM, U5.DS
  N11: パーツ1.D6_PWM, U5.SH_CP, U6.SH_CP
  N12: パーツ1.D7, U5.ST_CP, U6.ST_CP
  VCC: パーツ1.5V, U1.MR, U1.VCC, U2.MR, U2.VCC, U3.MR, U3.VCC, U4.MR, U4.VCC, U5.MR, U5.VCC, U6.MR, U6.VCC, U7.MR, U7.VCC, U8.MR, U8.VCC
  GND: パーツ1.GND, U1.GND, U1.OE, U2.GND, U2.OE, U3.GND, U3.OE, U4.GND, U4.OE, U5.GND, U5.OE, U6.GND, U6.OE, U7.GND, U7.OE, U8.GND, U8.OE, LED1.cathode, LED2.cathode, LED3.cathode, LED4.cathode, LED5.cathode, LED6.cathode, LED7.cathode, LED8.cathode, LED9.cathode, LED10.cathode, LED11.cathode, LED12.cathode, LED13.cathode, LED14.cathode, LED15.cathode, LED16.cathode, LED17.cathode, LED18.cathode, LED19.cathode, LED20.cathode, LED21.cathode, LED22.cathode, LED23.cathode, LED24.cathode, LED25.cathode, LED26.cathode, LED27.cathode, LED28.cathode, LED29.cathode, LED30.cathode, LED31.cathode, LED32.cathode, LED33.cathode, LED34.cathode, LED35.cathode, LED36.cathode, LED37.cathode, LED38.cathode, LED39.cathode, LED40.cathode
  N13: U1.Q1, R2.Pin_0
  N14: U1.Q2, R3.Pin_0
  N15: U1.Q3, R4.Pin_0
  N16: U1.Q4, R5.Pin_0
  N17: U1.Q5, R6.Pin_0
  N18: U1.Q6, R7.Pin_0
  N19: U1.Q7, R8.Pin_0
  N20: U1.Q7', U2.DS
  N21: U1.Q0, R1.Pin_0
  N22: U2.Q1, R10.Pin_0
  N23: U2.Q0, R9.Pin_0
  N24: R1.Pin_1, LED1.anode
  N25: R2.Pin_1, LED2.anode
  N26: R3.Pin_1, LED3.anode
  N27: R4.Pin_1, LED4.anode
  N28: R5.Pin_1, LED5.anode
  N29: R6.Pin_1, LED6.anode
  N30: R7.Pin_1, LED7.anode
  N31: R8.Pin_1, LED8.anode
  N32: R9.Pin_1, LED9.anode
  N33: R10.Pin_1, LED10.anode
  N34: R11.Pin_0, U3.Q0
  N35: R11.Pin_1, LED11.anode
  N36: R12.Pin_0, U3.Q1
  N37: R12.Pin_1, LED12.anode
  N38: R13.Pin_0, U3.Q2
  N39: R13.Pin_1, LED13.anode
  N40: R14.Pin_0, U3.Q3
  N41: R14.Pin_1, LED14.anode
  N42: R15.Pin_0, U3.Q4
  N43: R15.Pin_1, LED15.anode
  N44: R16.Pin_0, U3.Q5
  N45: R16.Pin_1, LED16.anode
  N46: R17.Pin_0, U3.Q6
  N47: R17.Pin_1, LED17.anode
  N48: R18.Pin_0, U3.Q7
  N49: R18.Pin_1, LED18.anode
  N50: U3.Q7', U4.DS
  N51: U4.Q1, R20.Pin_0
  N52: U4.Q0, R19.Pin_0
  N53: R19.Pin_1, LED19.anode
  N54: R20.Pin_1, LED20.anode
  N55: R21.Pin_0, U5.Q0
  N56: R21.Pin_1, LED21.anode
  N57: R22.Pin_0, U5.Q1
  N58: R22.Pin_1, LED22.anode
  N59: R23.Pin_0, U5.Q2
  N60: R23.Pin_1, LED23.anode
  N61: R24.Pin_0, U5.Q3
  N62: R24.Pin_1, LED24.anode
  N63: R25.Pin_0, U5.Q4
  N64: R25.Pin_1, LED25.anode
  N65: R26.Pin_0, U5.Q5
  N66: R26.Pin_1, LED26.anode
  N67: R27.Pin_0, U5.Q6
  N68: R27.Pin_1, LED27.anode
  N69: R28.Pin_0, U5.Q7
  N70: R28.Pin_1, LED28.anode
  N71: U5.Q7', U6.DS
  N72: U6.Q1, R30.Pin_0
  N73: U6.Q0, R29.Pin_0
  N74: R29.Pin_1, LED29.anode
  N75: R30.Pin_1, LED30.anode
  N76: R31.Pin_0, U7.Q0
  N77: R31.Pin_1, LED31.anode
  N78: R32.Pin_0, U7.Q1
  N79: R32.Pin_1, LED32.anode
  N80: R33.Pin_0, U7.Q2
  N81: R33.Pin_1, LED33.anode
  N82: R34.Pin_0, U7.Q3
  N83: R34.Pin_1, LED34.anode
  N84: R35.Pin_0, U7.Q4
  N85: R35.Pin_1, LED35.anode
  N86: R36.Pin_0, U7.Q5
  N87: R36.Pin_1, LED36.anode
  N88: R37.Pin_0, U7.Q6
  N89: R37.Pin_1, LED37.anode
  N90: R38.Pin_0, U7.Q7
  N91: R38.Pin_1, LED38.anode
  N92: U7.Q7', U8.DS
  N93: U8.Q1, R40.Pin_0
  N94: U8.Q0, R39.Pin_0
  N95: R39.Pin_1, LED39.anode
  N96: R40.Pin_1, LED40.anode
